// Digital circuit JK.dig as structural Verilog
module JK (
  input  J,
  input  Clk,
  input  K
);

  wire nand_1_out, nand_2_out, nand_3_out, nand_4_out;

  nand nand_1 (nand_1_out, nand_4_out, J, Clk);
  nand nand_2 (nand_2_out, Clk, K, nand_3_out);
  nand nand_3 (nand_3_out, nand_1_out, nand_4_out);
  nand nand_4 (nand_4_out, nand_3_out, nand_2_out);
  LED Q (.in(nand_3_out));
  LED Q_2 (.in(nand_4_out));
endmodule
